// Logisim project Q2.circ as structural Verilog: 1 circuit, main circuit main
module main (
  input  x,
  input  y,
  input  z,
  output A,
  output B,
  output C
);

  wire and_1_out, and_2_out, and_3_out, and_4_out, and_5_out, and_6_out, and_7_out, not_1_out, not_2_out,
       not_3_out;

  not not_1 (not_1_out, x);
  not not_2 (not_2_out, y);
  not not_3 (not_3_out, z);
  and and_1 (and_1_out, y, z);
  or or_1 (A, and_1_out, and_2_out);
  and and_2 (and_2_out, x, y);
  and and_3 (and_3_out, not_2_out, z);
  and and_4 (and_4_out, not_1_out, y, not_3_out);
  or or_2 (B, and_3_out, and_4_out, and_5_out);
  and and_5 (and_5_out, x, not_2_out);
  and and_6 (and_6_out, not_1_out, not_3_out);
  or or_3 (C, and_6_out, and_7_out);
  and and_7 (and_7_out, x, z);
endmodule
